// Digital circuit Control Unit.dig as structural Verilog
module Control_Unit (
  input  [15:0] IR,
  input  CLK,
  input  S,
  input  R,
  input  I,
  input  IEN,
  input  FGI,
  input  FGO,
  input  E,
  input  [15:0] AC,
  input  [15:0] DR,
  input  C_OUT,
  output [6:0] X,
  output S_CLR,
  output I_LD,
  output I_D,
  output R_J,
  output R_K,
  output IEN_J,
  output IEN_K,
  output FGI_K,
  output FGO_K,
  output AR_LD,
  output AR_INR,
  output AR_CLR,
  output MEM_read,
  output MEM_write,
  output PC_LD,
  output PC_INCR,
  output PC_CLR,
  output DR_LD,
  output DR_INCR,
  output AC_LD,
  output AC_INR,
  output AC_CLR,
  output [6:0] AL_OP,
  output OUTR_LD,
  output IR_LD,
  output TR_LD,
  output [15:0] T,
  output [7:0] D,
  output E_J,
  output E_K
);

  wire and_2_out, and_3_out, and_4_out, and_5_out, and_7_out, and_8_out, and_9_out, and_10_out, and_11_out,
       and_12_out, and_13_out, and_14_out, and_27_out, and_28_out, and_29_out, and_30_out, and_31_out,
       and_32_out, and_33_out, and_37_out, and_38_out, and_39_out, and_47_out, and_48_out, and_49_out,
       and_50_out, and_51_out, and_52_out, and_53_out, and_54_out, and_55_out, and_56_out, and_57_out,
       and_58_out, and_59_out, and_60_out, and_61_out, and_62_out, and_63_out, and_64_out, and_65_out,
       and_67_out, and_68_out, and_71_out, and_72_out, and_73_out, and_74_out, and_75_out, and_76_out,
       and_77_out, and_78_out, and_79_out, and_80_out, and_81_out, and_82_out, and_83_out, and_84_out,
       and_85_out, and_86_out, and_87_out, and_88_out, and_89_out, and_90_out, and_91_out, and_92_out,
       and_93_out, and_94_out, and_95_out, and_97_out, and_98_out, comparator_1_eq, comparator_2_eq,
       comparator_3_eq, comparator_4_eq, comparator_5_eq, driver_1_out, driver_2_out, driver_3_out,
       driver_4_out, driver_5_out, driver_6_out, driver_7_out, not_1_out, not_2_out, not_3_out, not_4_out,
       not_5_out, not_6_out, not_7_out, not_8_out, not_9_out, not_10_out, not_11_out, not_12_out, not_13_out,
       not_14_out, not_15_out, not_16_out, or_2_out, p, pulldown_2_out, pulldown_4_out, r_t_t, SC_clr;
  wire [3:0] SC;

  and and_1 (DR_INCR, D[6], T[5]);
  and and_2 (and_2_out, D[0], T[4]);
  and and_3 (and_3_out, D[1], T[4]);
  and and_4 (and_4_out, D[2], T[4]);
  and and_5 (and_5_out, D[6], T[4]);
  Counter #(.Bits(4)) u_SC (.en(S), .C(CLK), .clr(SC_clr), .out(SC));  // open: ovf
  or or_1 (DR_LD, and_2_out, and_3_out, and_4_out, and_5_out);
  and and_6 (p, D[7], IR[15], T[3]);
  Decoder #(.Selector_Bits(4)) decoder_1 (
    .sel(SC), .out_0(T[0]), .out_1(T[1]), .out_2(T[2]), .out_3(T[3]), .out_4(T[4]), .out_5(T[5]),
    .out_6(T[6]), .out_7(T[7]), .out_8(T[8]), .out_9(T[9]), .out_10(T[10]), .out_11(T[11]), .out_12(T[12]),
    .out_13(T[13]), .out_14(T[14]), .out_15(T[15]));
  or or_2 (or_2_out, FGI, FGO);
  and and_7 (and_7_out, D[0], T[5]);
  and and_8 (and_8_out, D[1], T[5]);
  and and_9 (and_9_out, D[2], T[5]);
  and and_10 (and_10_out, D[3], T[4]);
  and and_11 (and_11_out, D[4], T[4]);
  and and_12 (and_12_out, D[5], T[5]);
  and and_13 (and_13_out, D[6], T[6]);
  and and_14 (and_14_out, R_J, T[2]);
  not not_1 (not_1_out, IR[15]);
  and and_15 (AL_OP[0], D[0], T[5]);
  and and_16 (AL_OP[1], D[1], T[5]);
  and and_17 (AL_OP[2], D[2], T[5]);
  and and_18 (AL_OP[3], p, IR[11]);
  and and_19 (AL_OP[4], r_t_t, IR[9]);
  and and_20 (AL_OP[5], r_t_t, IR[7]);
  and and_21 (AL_OP[6], r_t_t, IR[6]);
  Decoder #(.Selector_Bits(3)) decoder_2 (
    .sel(IR[14:12]), .out_0(D[0]), .out_1(D[1]), .out_2(D[2]), .out_3(D[3]), .out_4(D[4]), .out_5(D[5]),
    .out_6(D[6]), .out_7(D[7]));
  and and_22 (r_t_t, D[7], not_1_out, T[3]);
  and and_23 (R_J, or_2_out, IEN, T[0], T[1], T[2]);
  or or_3 (SC_clr, and_7_out, and_8_out, and_9_out, and_10_out, and_11_out, and_12_out, and_13_out, and_14_out, p, r_t_t);
  not not_2 (not_2_out, D[7]);
  not not_3 (not_3_out, R_J);
  not not_4 (not_4_out, R_J);
  and and_24 (FGI_K, p, IR[11]);
  and and_25 (FGO_K, p, IR[10]);
  and and_26 (IEN_J, p, IR[7]);
  and and_27 (and_27_out, IR[6], p);
  and and_28 (and_28_out, R_J, T[2]);
  and and_29 (and_29_out, r_t_t, IR[10]);
  and and_30 (and_30_out, D[1], T[5]);
  and and_31 (and_31_out, r_t_t, IR[8]);
  and and_32 (and_32_out, r_t_t, IR[6]);
  and and_33 (and_33_out, r_t_t, IR[7]);
  and and_34 (IR_LD, not_3_out, T[1]);
  and and_35 (TR_LD, R_J, T[0]);
  and and_36 (OUTR_LD, p, IR[10]);
  or or_4 (IEN_K, and_27_out, and_28_out);
  not not_5 (not_5_out, AC[15]);
  not not_6 (not_6_out, AC[0]);
  assign driver_1_out = and_29_out ? 1'b0 : 1'bz;  // Driver driver_1
  assign driver_2_out = and_30_out ? C_OUT : 1'bz;  // Driver driver_2
  not not_7 (not_7_out, C_OUT);
  assign driver_3_out = and_31_out ? 1'b1 : 1'bz;  // Driver driver_3
  assign driver_4_out = and_32_out ? AC[15] : 1'bz;  // Driver driver_4
  assign driver_5_out = and_32_out ? not_5_out : 1'bz;  // Driver driver_5
  assign driver_6_out = and_33_out ? AC[0] : 1'bz;  // Driver driver_6
  assign driver_7_out = and_33_out ? not_6_out : 1'bz;  // Driver driver_7
  and and_37 (and_37_out, not_2_out, IR[15], T[3]);
  and and_38 (and_38_out, not_4_out, T[0]);
  and and_39 (and_39_out, not_4_out, T[2]);
  PullDown pulldown_1 (.out(driver_1_out));
  PullDown pulldown_2 (.out(pulldown_2_out));
  assign pulldown_2_out = and_29_out ? 1'b1 : 1'bz;  // Driver driver_8
  PullDown pulldown_3 (.out(driver_2_out));
  PullDown pulldown_4 (.out(pulldown_4_out));
  assign pulldown_4_out = and_30_out ? not_7_out : 1'bz;  // Driver driver_9
  PullDown pulldown_5 (.out(driver_3_out));
  PullDown pulldown_6 (.out(driver_4_out));
  PullDown pulldown_7 (.out(driver_5_out));
  PullDown pulldown_8 (.out(driver_6_out));
  PullDown pulldown_9 (.out(driver_7_out));
  not not_8 (not_8_out, R_J);
  not not_9 (not_9_out, R_J);
  and and_40 (AR_INR, D[5], T[4]);
  and and_41 (AR_CLR, R_J, T[0]);
  or or_5 (AR_LD, and_37_out, and_38_out, and_39_out);
  and and_42 (R_K, not_8_out, T[2]);
  and and_43 (I_LD, not_9_out, T[2]);
  and and_44 (S_CLR, r_t_t, IR[0]);
  or or_6 (E_J, driver_1_out, driver_2_out, driver_3_out, driver_4_out, driver_6_out);
  or or_7 (E_K, pulldown_2_out, pulldown_4_out, driver_3_out, driver_5_out, driver_7_out);
  and and_45 (AC_INR, r_t_t, IR[5]);
  and and_46 (AC_CLR, r_t_t, IR[11]);
  not not_10 (not_10_out, D[7]);
  not not_11 (not_11_out, R_J);
  and and_47 (and_47_out, D[3], T[4]);
  and and_48 (and_48_out, D[5], T[4]);
  and and_49 (and_49_out, D[6], T[6]);
  and and_50 (and_50_out, R_J, T[1]);
  and and_51 (and_51_out, D[0], T[4]);
  and and_52 (and_52_out, D[1], T[4]);
  and and_53 (and_53_out, D[2], T[4]);
  and and_54 (and_54_out, D[6], T[4]);
  and and_55 (and_55_out, not_10_out, IR[15], T[3]);
  and and_56 (and_56_out, not_11_out, T[1]);
  or or_8 (MEM_write, and_47_out, and_48_out, and_49_out, and_50_out);
  and and_57 (and_57_out, IR[11], p);
  and and_58 (and_58_out, IR[6], r_t_t);
  and and_59 (and_59_out, IR[7], r_t_t);
  and and_60 (and_60_out, IR[9], r_t_t);
  and and_61 (and_61_out, D[0], T[5]);
  and and_62 (and_62_out, D[1], T[5]);
  and and_63 (and_63_out, D[2], T[5]);
  or or_9 (MEM_read, and_51_out, and_52_out, and_53_out, and_54_out, and_55_out, and_56_out);
  or or_10 (AC_LD, and_57_out, and_58_out, and_59_out, and_60_out, and_61_out, and_62_out, and_63_out);
  and and_64 (and_64_out, D[4], T[4]);
  and and_65 (and_65_out, D[5], T[5]);
  and and_66 (X[5], R_J, T[1]);
  or or_11 (PC_LD, and_64_out, and_65_out);
  and and_67 (and_67_out, IR[10], p);
  and and_68 (and_68_out, D[3], T[4]);
  not not_12 (not_12_out, R_J);
  and and_69 (X[4], not_12_out, T[2]);
  not not_13 (not_13_out, D[7]);
  not not_14 (not_14_out, R_J);
  or or_12 (X[3], and_67_out, and_68_out);
  not not_15 (not_15_out, R_J);
  and and_70 (X[2], D[6], T[6]);
  and and_71 (and_71_out, D[0], T[4]);
  and and_72 (and_72_out, D[1], T[4]);
  and and_73 (and_73_out, D[2], T[4]);
  and and_74 (and_74_out, D[6], T[4]);
  and and_75 (and_75_out, not_13_out, IR[15], T[3]);
  and and_76 (and_76_out, not_15_out, T[1]);
  and and_77 (and_77_out, IR[1], r_t_t);
  and and_78 (and_78_out, IR[2], r_t_t);
  and and_79 (and_79_out, IR[3], r_t_t);
  and and_80 (and_80_out, IR[4], r_t_t);
  and and_81 (and_81_out, IR[8], p);
  and and_82 (and_82_out, IR[9], p);
  and and_83 (and_83_out, D[6], T[6]);
  and and_84 (and_84_out, not_14_out, T[1]);
  and and_85 (and_85_out, R_J, T[2]);
  not not_16 (not_16_out, R_J);
  or or_13 (X[6], and_71_out, and_72_out, and_73_out, and_74_out, and_75_out, and_76_out);
  Comparator comparator_1 (.a(1'b0), .b(E), .eq(comparator_1_eq));  // open: gt, lt
  Comparator #(.Bits(16)) comparator_2 (.a({16{1'b0}}), .b(AC), .eq(comparator_2_eq));  // open: gt, lt
  Comparator comparator_3 (.a(1'b1), .b(AC[15]), .eq(comparator_3_eq));  // open: gt, lt
  Comparator comparator_4 (.a(1'b0), .b(AC[15]), .eq(comparator_4_eq));  // open: gt, lt
  Comparator #(.Bits(16)) comparator_5 (.a({16{1'b0}}), .b(DR), .eq(comparator_5_eq));  // open: gt, lt
  and and_86 (and_86_out, comparator_2_eq, and_78_out);
  and and_87 (and_87_out, FGI, and_82_out);
  and and_88 (and_88_out, D[5], T[4]);
  and and_89 (and_89_out, not_16_out, T[0]);
  and and_90 (and_90_out, R_J, T[0]);
  and and_91 (and_91_out, comparator_1_eq, and_77_out);
  and and_92 (and_92_out, comparator_3_eq, and_79_out);
  and and_93 (and_93_out, comparator_4_eq, and_80_out);
  and and_94 (and_94_out, FGO, and_81_out);
  and and_95 (and_95_out, comparator_5_eq, and_83_out);
  or or_14 (X[1], and_88_out, and_89_out, and_90_out);
  and and_96 (PC_CLR, R_J, T[1]);
  or or_15 (PC_INCR, and_91_out, and_86_out, and_92_out, and_93_out, and_94_out, and_87_out, and_95_out, and_84_out, and_85_out);
  and and_97 (and_97_out, D[4], T[4]);
  and and_98 (and_98_out, D[5], T[5]);
  or or_16 (X[0], and_97_out, and_98_out);

  assign I_D = IR[15];

  // Other names for the same wires on the sheet: AC_0 = AC[0]; AC_15 = AC[15]; D_0 = D[0]; D_1 = D[1]; D_2 = D[2];
  //   D_3 = D[3]; D_4 = D[4]; D_5 = D[5]; D_6 = D[6]; D_7 = D[7]; I_old = I; Adress[11:0] = IR[11:0]; B_0 = IR[0];
  //   B_1 = IR[1]; B_2 = IR[2]; B_3 = IR[3]; B_4 = IR[4]; B_5 = IR[5]; B_6 = IR[6]; B_7 = IR[7]; B_8 = IR[8];
  //   B_9 = IR[9]; B_10 = IR[10]; B_11 = IR[11]; D_bits[2:0] = IR[14:12]; I_t = IR[15]; R_old = R; R_t = R_J;
  //   T_0 = T[0]; T_1 = T[1]; T_2 = T[2]; T_3 = T[3]; T_4 = T[4]; T_5 = T[5]; T_6 = T[6]; T_7 = T[7]; T_8 = T[8];
  //   T_9 = T[9]; T_10 = T[10]; T_11 = T[11]; T_12 = T[12]; T_13 = T[13]; T_14 = T[14]; T_15 = T[15]

  // Notes on the sheet:
  //   Inputs
  //   DR control
  //   SC clear
  //   IR Decode and SC Timing signals
  //   R, r and p
  //   AL operations
  //   AR control
  //   Flags
  //   IR control
  //   TR control
  //   OUTR control
  //   Memory control
  //   AC control
  //   D and T output
  //   PC control
  //   BUS control
  //   IR
  //   TR
  //   RAM
  //   AC
  //   DR
  //   AR
  //   PC
endmodule
